// Logisim project CISC_CPU.circ as structural Verilog: 4 circuits, main circuit Main
module CPU (
  input  [31:0] Sec_instruction,
  input  direct_input,
  input  [31:0] ReadFromRAM,
  input  CLK,
  input  [15:0] primary_instruc,
  output [31:0] Reminder,
  output [15:0] Address_Bus,
  output [1:0] Control_bus,
  output [31:0] WriteOnRAM
);

  wire alu_1_zero_flag, and_1_out, decode, en_R_fromGPR_toALU, en_R_FromRAM, en_W_OnGPR, execute, fetch,
       or_2_out, Overflow, Sec_instruc_address_orNumber;
  wire [1:0] instruction_inputA, instruction_inputB;
  wire [2:0] controlled_buffer_1_out;
  wire [3:0] opCode;
  wire [15:0] control_unit_1_instruction, multiplexer_2_out;
  wire [31:0] alu_1_alu_output, control_unit_1_toalu_outa, control_unit_1_toalu_outb, multiplexer_1_out;

  and and_1 (and_1_out, execute, en_R_FromRAM);
  or or_1 (Control_bus[1], fetch, and_1_out);
  ALU alu_1 (
    .op_code(opCode), .Input_B(control_unit_1_toalu_outb), .Input_A(control_unit_1_toalu_outa),
    .ALU_Output(alu_1_alu_output), .Multi_Div_reminder(Reminder), .Overflow_Flag(Overflow),
    .Zero_flag(alu_1_zero_flag));
  Multiplexer #(.width(32)) multiplexer_1 (
    .in0(alu_1_alu_output), .in1(Sec_instruction), .out(multiplexer_1_out), .sel(direct_input));
  or or_2 (or_2_out, decode, execute);
  Control_Unit control_unit_1 (
    .op_code(opCode), .en_W_onGPR(en_W_OnGPR), .Input_from_RAM(ReadFromRAM), .Overflow_flag(Overflow),
    .FromALU(multiplexer_1_out), .en_W_onRAM(Control_bus[0]), .CLK(CLK),
    .en_R_fromGPRtoALU(en_R_fromGPR_toALU), .enable_read_from_RAM(Control_bus[1]),
    .Sec_instruction_addressOrNumber(Sec_instruc_address_orNumber),
    .GPR_inputB_toALUorRAM(instruction_inputB), .GPRinputAtoALU_or_FromALUorRAM(instruction_inputA),
    .ZeroFlag(alu_1_zero_flag), .instruction(control_unit_1_instruction), .Address_bus(Address_Bus),
    .fetch(fetch), .decode(decode), .execute(execute), .toALU_outA(control_unit_1_toalu_outa),
    .toALU_outB(control_unit_1_toalu_outb), .out_to_RAM(WriteOnRAM));
  Multiplexer #(.width(16)) multiplexer_2 (
    .in0(control_unit_1_instruction), .in1(primary_instruc), .out(multiplexer_2_out), .sel(direct_input));
  assign {opCode, en_W_OnGPR, en_R_fromGPR_toALU, instruction_inputA, instruction_inputB, Sec_instruc_address_orNumber, Control_bus[0], en_R_FromRAM, controlled_buffer_1_out} = or_2_out ? multiplexer_2_out : 16'bz;  // Controlled_Buffer controlled_buffer_1

  // Other names for the same wires on the sheet: en_W_onRAM = Control_bus[0]; getRAM = Control_bus[1]
endmodule

module ALU (
  input  [31:0] Input_A,
  input  [31:0] Input_B,
  input  [3:0] op_code,
  output [31:0] ALU_Output,
  output [31:0] Multi_Div_reminder,
  output Zero_flag,
  output Overflow_Flag
);

  wire nor_1_out, or_2_out, Sub_borrow, Sum_carry;
  wire [31:0] adder_1_out, and_1_out, div_borrow, divider_1_out, multi_carry, multiplexer_1_out,
       multiplier_1_out, or_1_out, shifter_1_out, shifter_2_out, subtractor_1_out;

  Adder #(.width(32)) adder_1 (.a(Input_A), .b(Input_B), .out(adder_1_out), .cout(Sum_carry));  // open: cin
  Subtractor #(.width(32)) subtractor_1 (
    .a(Input_A), .b(Input_B), .out(subtractor_1_out), .bout(Sub_borrow));  // open: bin
  Multiplier #(.width(32)) multiplier_1 (
    .a(Input_A), .b(Input_B), .out(multiplier_1_out), .cout(multi_carry));  // open: cin
  Divider #(.width(32)) divider_1 (.a(Input_A), .b(Input_B), .out(divider_1_out), .rem(div_borrow));  // open: upper
  Shifter #(.width(32)) shifter_1 (.in(Input_A), .\dist (Input_B[4:0]), .out(shifter_1_out));
  Shifter #(.shift("lr"), .width(32)) shifter_2 (.in(Input_A), .\dist (Input_B[4:0]), .out(shifter_2_out));
  assign and_1_out = Input_A & Input_B;  // AND_Gate and_1, 32 bits wide
  assign or_1_out = Input_A | Input_B;  // OR_Gate or_1, 32 bits wide
  Multiplexer #(.select(3), .width(32)) multiplexer_1 (
    .in0(adder_1_out), .in1(subtractor_1_out), .in2(multiplier_1_out), .in3(divider_1_out),
    .in4(shifter_1_out), .in5(shifter_2_out), .in6(and_1_out), .in7(or_1_out), .out(multiplexer_1_out),
    .sel(op_code[2:0]));
  or or_2 (or_2_out, Sum_carry, Sub_borrow);
  nor nor_1 (nor_1_out, op_code[2], op_code[1]);
  Multiplexer #(.width(32)) multiplexer_2 (.in0(multiplexer_1_out), .in1(Input_B), .out(ALU_Output), .sel(op_code[3]));
  and and_2 (Overflow_Flag, or_2_out, nor_1_out);
  Multiplexer #(.select(3), .width(32)) multiplexer_3 (
    .in0({32{1'b0}}), .in1({32{1'b0}}), .in2(multi_carry), .in3(div_borrow), .in4({32{1'b0}}),
    .in5({32{1'b0}}), .in6({32{1'b0}}), .in7({32{1'b0}}), .out(Multi_Div_reminder), .sel(op_code[2:0]));
  nor nor_2 (Zero_flag, multiplexer_1_out[15], multiplexer_1_out[0], multiplexer_1_out[1], multiplexer_1_out[2], multiplexer_1_out[3], multiplexer_1_out[4], multiplexer_1_out[5], multiplexer_1_out[6], multiplexer_1_out[7], multiplexer_1_out[8], multiplexer_1_out[9], multiplexer_1_out[10], multiplexer_1_out[11], multiplexer_1_out[12], multiplexer_1_out[13], multiplexer_1_out[14], multiplexer_1_out[16], multiplexer_1_out[17], multiplexer_1_out[18], multiplexer_1_out[19], multiplexer_1_out[20], multiplexer_1_out[21], multiplexer_1_out[22], multiplexer_1_out[23], multiplexer_1_out[24], multiplexer_1_out[25], multiplexer_1_out[26], multiplexer_1_out[27], multiplexer_1_out[28], multiplexer_1_out[29], multiplexer_1_out[30], multiplexer_1_out[31]);

  // Other names for the same wires on the sheet: Mov_operation = op_code[3]; Opcode[2:0] = op_code[2:0]
endmodule

module Control_Unit (
  input  [1:0] GPRinputAtoALU_or_FromALUorRAM,
  input  [1:0] GPR_inputB_toALUorRAM,
  input  [31:0] Input_from_RAM,
  input  [31:0] FromALU,
  input  enable_read_from_RAM,
  input  en_W_onRAM,
  input  Sec_instruction_addressOrNumber,
  input  CLK,
  input  en_R_fromGPRtoALU,
  input  en_W_onGPR,
  input  [3:0] op_code,
  input  Overflow_flag,
  input  ZeroFlag,
  output [31:0] toALU_outA,
  output [31:0] toALU_outB,
  output [31:0] out_to_RAM,
  output [15:0] instruction,
  output [15:0] Address_bus,
  output fetch,
  output decode,
  output execute
);

  wire and_1_out, and_4_out, and_5_out, and_6_out, and_7_out, and_8_out, and_9_out, and_10_out,
       controlled_buffer_1_out, controlled_buffer_4_out, g_than, L_than, multiplexer_2_out, nor_1_out, NZF,
       or_1_out, or_2_out, or_3_out, s_Ax, s_Bx, s_Cx, s_Dx, shift_register_1_p1, shift_register_1_p5,
       shift_register_1_p6, ZF;
  wire [2:0] multiplexer_1_out;
  wire [15:0] adder_1_out, controlled_buffer_2_out, controlled_buffer_2_out_2, controlled_buffer_3_out,
       Instruction_ptr_q, multiplexer_3_out, sec_instruc_reg_q, sec_instruction;
  wire [31:0] Accumlator_q, Ax_q, Bx, Cx, Dx, multiplexer_4_out, multiplexer_5_out, multiplexer_6_out,
       multiplexer_7_out;

  // Shift_Register #(.length(3)) shift_register_1: pin names not known; wires that end beside it: shift_register_1_p1, CLK, CLK, 1'b1, shift_register_1_p5, shift_register_1_p6, execute
  Demultiplexer #(.select(2)) demultiplexer_1 (
    .out0(s_Ax), .out1(s_Bx), .out2(s_Cx), .out3(s_Dx), .in(en_W_onGPR), .sel(GPRinputAtoALU_or_FromALUorRAM));
  D_Flip_Flop #(.trigger("low")) d_ff_1 (
    .D(execute), .clk(CLK), .Q(shift_register_1_p1), .reset(and_1_out));  // open: Qn, preset
  and and_1 (and_1_out, execute, ~CLK);  // AND_Gate
  D_Flip_Flop #(.trigger("falling")) d_ff_2 (
    .D(controlled_buffer_1_out), .clk(CLK), .Q(L_than), .Qn(g_than));  // open: preset, reset
  assign controlled_buffer_1_out = execute ? Overflow_flag : 1'bz;  // Controlled_Buffer controlled_buffer_1
  assign {controlled_buffer_2_out, controlled_buffer_2_out_2} = nor_1_out ? FromALU : 32'bz;  // Controlled_Buffer controlled_buffer_2
  nor nor_1 (nor_1_out, enable_read_from_RAM, en_W_onRAM);
  and and_2 (fetch, shift_register_1_p5, ~shift_register_1_p6, ~execute);  // AND_Gate
  and and_3 (decode, shift_register_1_p6, ~execute);  // AND_Gate
  Multiplexer #(.width(3)) multiplexer_1 (.in0(3'b000), .in1(op_code[2:0]), .out(multiplexer_1_out), .sel(op_code[3]));
  Register #(.trigger("falling"), .width(32)) Accumlator (
    .D({controlled_buffer_2_out, controlled_buffer_2_out_2}), .en(decode), .clk(CLK), .Q(Accumlator_q));  // open: clr
  Multiplexer #(.select(3)) multiplexer_2 (
    .in0(1'b0), .in1(1'b1), .in2(ZF), .in3(NZF), .in4(L_than), .in5(g_than), .out(multiplexer_2_out),
    .sel(multiplexer_1_out));  // open: in6, in7
  Adder #(.width(16)) adder_1 (.a(Instruction_ptr_q), .b(16'h1), .out(adder_1_out));  // open: cin, cout
  assign controlled_buffer_3_out = execute ? controlled_buffer_2_out_2 : 16'bz;  // Controlled_Buffer controlled_buffer_3
  Multiplexer #(.width(16)) multiplexer_3 (
    .in0(adder_1_out), .in1(controlled_buffer_3_out), .out(multiplexer_3_out), .sel(multiplexer_2_out));
  D_Flip_Flop #(.trigger("falling")) d_ff_3 (
    .D(controlled_buffer_4_out), .clk(CLK), .Q(ZF), .Qn(NZF));  // open: preset, reset
  assign controlled_buffer_4_out = execute ? ZeroFlag : 1'bz;  // Controlled_Buffer controlled_buffer_4
  Register #(.trigger("falling"), .width(32)) Ax (.D(Accumlator_q), .en(and_4_out), .clk(CLK), .Q(Ax_q));  // open: clr
  and and_4 (and_4_out, s_Ax, execute);
  Register #(.trigger("falling"), .width(32)) u_Bx (.D(Accumlator_q), .en(and_5_out), .clk(CLK), .Q(Bx));  // open: clr
  and and_5 (and_5_out, s_Bx, execute);
  Register #(.trigger("falling"), .width(32)) u_Cx (.D(Accumlator_q), .en(and_6_out), .clk(CLK), .Q(Cx));  // open: clr
  and and_6 (and_6_out, s_Cx, execute);
  Register #(.trigger("falling"), .width(32)) u_Dx (.D(Accumlator_q), .en(and_7_out), .clk(CLK), .Q(Dx));  // open: clr
  and and_7 (and_7_out, s_Dx, execute);
  Register #(.trigger("falling"), .width(16)) first_instruc_reg (
    .D(controlled_buffer_2_out), .en(fetch), .clk(CLK), .Q(instruction), .clr(shift_register_1_p1));
  Register #(.trigger("falling"), .width(16)) sec_instruc_reg (
    .D(controlled_buffer_2_out_2), .en(fetch), .clk(CLK), .Q(sec_instruc_reg_q), .clr(shift_register_1_p1));
  Register #(.trigger("falling"), .width(16)) Instruction_ptr (
    .D(multiplexer_3_out), .en(execute), .clk(CLK), .Q(Instruction_ptr_q));  // open: clr
  assign {controlled_buffer_2_out, controlled_buffer_2_out_2} = and_8_out ? Input_from_RAM : 32'bz;  // Controlled_Buffer controlled_buffer_5
  and and_8 (and_8_out, enable_read_from_RAM, ~en_W_onRAM);  // AND_Gate
  assign sec_instruction = or_1_out ? sec_instruc_reg_q : 16'bz;  // Controlled_Buffer controlled_buffer_6
  or or_1 (or_1_out, decode, execute);
  assign Address_bus = or_2_out ? Instruction_ptr_q : 16'bz;  // Controlled_Buffer controlled_buffer_7
  or or_2 (or_2_out, fetch, multiplexer_2_out);
  Multiplexer #(.select(2), .width(32)) multiplexer_4 (
    .in0(Ax_q), .in1(Bx), .in2(Cx), .in3(Dx), .out(multiplexer_4_out), .sel(GPRinputAtoALU_or_FromALUorRAM));
  Multiplexer #(.select(2), .width(32)) multiplexer_5 (
    .in0(Ax_q), .in1(Bx), .in2(Cx), .in3(Dx), .out(multiplexer_5_out), .sel(GPR_inputB_toALUorRAM));
  Multiplexer #(.select(2), .width(32)) multiplexer_6 (
    .in0(Ax_q), .in1(Bx), .in2(Cx), .in3(Dx), .out(multiplexer_6_out), .sel(GPR_inputB_toALUorRAM));
  and and_9 (and_9_out, or_3_out, execute);
  assign Address_bus = and_9_out ? sec_instruction : 16'bz;  // Controlled_Buffer controlled_buffer_8
  Multiplexer #(.width(32)) multiplexer_7 (
    .in0(multiplexer_5_out), .in1({{16{1'b0}}, sec_instruction}), .out(multiplexer_7_out),
    .sel(Sec_instruction_addressOrNumber));
  or or_3 (or_3_out, en_W_onRAM, enable_read_from_RAM);
  assign out_to_RAM = and_10_out ? multiplexer_6_out : 32'bz;  // Controlled_Buffer controlled_buffer_9
  and and_10 (and_10_out, en_W_onRAM, en_R_fromGPRtoALU, ~enable_read_from_RAM);  // AND_Gate
  assign toALU_outA = en_R_fromGPRtoALU ? multiplexer_4_out : 32'bz;  // Controlled_Buffer controlled_buffer_10
  assign toALU_outB = en_R_fromGPRtoALU ? multiplexer_7_out : 32'bz;  // Controlled_Buffer controlled_buffer_11

  // Other names for the same wires on the sheet: en_GPR_R = en_R_fromGPRtoALU; get_RAM = enable_read_from_RAM;
  //   GPRinputA[1:0] = GPRinputAtoALU_or_FromALUorRAM; GPRinputB[1:0] = GPR_inputB_toALUorRAM; set_RAM = en_W_onRAM
endmodule

module Main (
  input  [15:0] primaryInput,
  input  [31:0] Secoundary_Iput,
  input  Direct_input
);

  wire CLK;
  wire [1:0] cpu_1_control_bus;
  wire [15:0] cpu_1_address_bus;
  wire [31:0] cpu_1_writeonram;

  Clock clock_1 (.out(CLK));
  CPU cpu_1 (
    .primary_instruc(primaryInput), .ReadFromRAM(cpu_1_writeonram), .direct_input(Direct_input),
    .Sec_instruction(Secoundary_Iput), .CLK(CLK), .Address_Bus(cpu_1_address_bus),
    .Control_bus(cpu_1_control_bus), .WriteOnRAM(cpu_1_writeonram));  // open: Reminder
  RAM #(.addrWidth(16), .dataWidth(32), .databus("bidir"), .enables("line"), .trigger("falling")) ram_1 (
    .addr(cpu_1_address_bus), .we(cpu_1_control_bus[0]), .oe(cpu_1_control_bus[1]), .clk(CLK),
    .data(cpu_1_writeonram));
endmodule
